// Logisim project JustInCase.circ as structural Verilog: 1 circuit, main circuit main
module main (
  input  A,
  input  B,
  input  C,
  input  D,
  output x
);

  wire and_1_out, and_2_out, not_1_out, not_2_out, not_3_out, not_4_out, or_1_out, or_2_out;

  not not_1 (not_1_out, A);
  not not_2 (not_2_out, B);
  not not_3 (not_3_out, C);
  not not_4 (not_4_out, D);
  or or_1 (or_1_out, B, not_3_out);
  or or_2 (or_2_out, not_1_out, D);
  and and_1 (and_1_out, A, not_2_out, C);
  and and_2 (and_2_out, not_4_out, A, or_1_out, or_2_out, not_2_out, C);
  or or_3 (x, and_1_out, and_2_out);
endmodule
